# Fritzing sketch Thermistor Conditioning (saved by Fritzing 0.7.10b)
breadboards: 1

parts:
  R_th = Temperature Sensor (Thermistor) [thermistor_type=NTC package=THT]
  R1 = Resistor [tolerance=±5% resistance=10k package=THT]
  R2 = Resistor [tolerance=±5% resistance=220 package=THT]
  R3 = Resistor [tolerance=±5% resistance=220 package=THT]
  R4 = Resistor [tolerance=±5% resistance=220 package=THT]
  U1 = LM 358 Dual Op-Amp [package="DIP8 [THT]"]
  R5 = Resistor [tolerance=±5% resistance=220 package=THT]
  R6 = Resistor [tolerance=±5% resistance=220 package=THT]

nets:
  N1: R_th.pin_0, R1.Pin_0, U1.connector2
  3.3V: R_th.pin_1, R2.Pin_0, U1.connector7
  GND: R1.Pin_1, R4.Pin_1, U1.connector3
  N2: R2.Pin_1, R3.Pin_0
  N3: R3.Pin_1, R4.Pin_0, R5.Pin_1
  N4: U1.connector0, R6.Pin_0
  N5: U1.connector1, R5.Pin_0, R6.Pin_1

notes:
  ND06P00103K
  10k
  22k
  120k
  56k
  Op-amp can run from 3.3V supply rail as it has very good rail-rail operation.
  MPC6231 Single Op-amp
  Vo to ADC
  Gain setting resistors could be knocked up a decade if current draw from ref. divider proves too high.
