# Fritzing sketch humiditysensor (saved by Fritzing 0.7.12b)
breadboards: 1

parts:
  part = Variable Capacitor [capacitance=100nF max_capacitance=10pF min_capacitance=2pF voltage=35V part_number="Humidity sensor"]
  R1 = 470 Ω Resistor [package=THT]
  Schottky_diode = Schottky Diode [package="Melf DO-213 AB [SMD]"]

nets:
  GND: part.0
  Sense: part.1, R1.Pin_1, Schottky_diode.anode
  Charge: R1.Pin_0, Schottky_diode.cathode
