# Fritzing sketch i2c (saved by Fritzing 0.7.12b)
breadboards: 1

parts:
  IC1 = 24LC256 [package=THT]
  R1 = Resistor [tolerance=±5% resistance=4.7k part_number=4k7 package=THT]
  R2 = Resistor [tolerance=±5% resistance=220 part_number=4k7 package=THT]
  IC2 = MMA7660FC [part_number=MMA7660FC package="DIP (Dual Inline) [THT]"]

nets:
  GND: IC1.A0, IC1.0V, IC1.WP_-_Write_Protect, IC2.RESERVED, IC2.AVSS, IC2.DVSS
  SDA: IC1.SDA_-_I2C_Data, R2.Pin_1, IC2.SDA
  SCL: IC1.SCL_-_I2C_Clock, R1.Pin_1, IC2.SCL
  3.3V: IC1.+V, R1.Pin_0, R2.Pin_0, IC2.AVDD, IC2.DVDD
  INT: IC2.!INT

custom parts:
  MMA7660FC: A DIP stand-in part for whatever IC you want. With 10 pins on a 300mil dual inline package (DIP) footprint.u
