# Fritzing sketch power (saved by Fritzing 0.7.12b)
breadboards: 1

parts:
  MCP1700 = Voltage Regulator - 5V [package="DPak [SMD]"]
  4x_AA_batteries = Battery block 9V
  1uF = Ceramic Capacitor [package=THT]
  C1 = Ceramic Capacitor [package=THT]

nets:
  N1: MCP1700.input_voltage, 4x_AA_batteries.+, 1uF.pin_1
  GND: MCP1700.GND, 4x_AA_batteries.-, 1uF.pin_0, C1.pin_0
  5V: MCP1700.output_voltage, C1.pin_1
